// Logisim project ß2015.circ as structural Verilog: 4 circuits, main circuit Control Unit
module \ß2015  (
  input  [4:0] DATA_IN,
  input  CLOCK,
  input  WAIT,
  input  RESET,
  output [4:0] ADDRESS,
  output MREQ,
  output READ,
  output IOREQ,
  output WR,
  output [4:0] DATA_OUT
);

  wire _0, _1, _2, _3, _4, _5, _6, _7, _8, _9, _10, _11, _12, _13, _14, _19, _20, _21, _22, _23, _24, _28,
       _29, alu_1_flag, alu_1_flag_z, and_1_out, controlled_buffer_6_out, controlled_buffer_7_out,
       controlled_buffer_8_out, FLAG_q, FLAG_Z_q, not_1_out, not_2_out,
       Test_disabilita_altra_entrata_1___no__0___si, Test_out;
  wire [4:0] A_q, alu_1_result, ALUREG_q, B_q, C_q, controlled_buffer_1_out, data_register_q,
       Instruction_Register_q, TEMP_q;
  wire [31:25] Control_Unit_control_output;

  LED led_1 (.in(_28));
  LED BUS__C (.in(_2));
  LED C__BUS (.in(_1));
  LED CU_RESET (.in(_14));
  LED DR__BUS (.in(_13));
  LED led_2 (.in(_29));
  Register #(.width(5), .trigger("falling")) Instruction_Register (
    .D(controlled_buffer_1_out), .Q(Instruction_Register_q), .clk(_11), .clr(RESET));  // open: en
  LED B__BUS (.in(_3));
  LED #(.active("false")) u_MREQ (.in(MREQ));
  and and_1 (and_1_out, WAIT, CLOCK);
  LED ALU1 (.in(_4));
  LED #(.active("false")) u_READ (.in(READ));
  LED A__A (.in(_5));
  LED BUS__A (.in(_6));
  LED #(.active("false")) u_IOREQ (.in(IOREQ));
  LED #(.active("false")) u_WR (.in(WR));
  Control_Unit Control_Unit (
    .Internal_clock(and_1_out), .Reset(_14), .Op_Code(Instruction_Register_q),
    .Control_Output({Control_Unit_control_output[31:30], _29, _28, Control_Unit_control_output[27:25], _24, _23, _22, _21, _20, _19, WR, IOREQ, READ, MREQ, _14, _13, _12, _11, _10, _9, _8, _7, _6, _5, _4, _3, _2, _1, _0}));  // open: CU_COUNTER
  Register #(.width(5)) A (.D(controlled_buffer_1_out), .Q(A_q), .clk(_6));  // open: en, clr
  Register #(.width(5)) B (.D(controlled_buffer_1_out), .Q(B_q), .clk(_21));  // open: en, clr
  assign controlled_buffer_1_out = _3 ? B_q : 5'bz;  // Controlled_Buffer controlled_buffer_1
  Register #(.width(5)) C (.D(controlled_buffer_1_out), .Q(C_q), .clk(_2));  // open: en, clr
  assign controlled_buffer_1_out = _5 ? A_q : 5'bz;  // Controlled_Buffer controlled_buffer_2
  assign controlled_buffer_1_out = _1 ? C_q : 5'bz;  // Controlled_Buffer controlled_buffer_3
  LED ALU__BUS (.in(_7));
  LED ALU__REG (.in(_19));
  ALU alu_1 (.OP1(A_q), .OP2(TEMP_q), .op({_8, _4}), .Flag(alu_1_flag), .Flag_z(alu_1_flag_z), .Result(alu_1_result));
  Register #(.width(5)) TEMP (.D(controlled_buffer_1_out), .Q(TEMP_q), .clk(_0));  // open: en, clr
  LED ALU0 (.in(_8));
  LED led_3 (.in(_20));
  assign controlled_buffer_1_out = _13 ? data_register_q : 5'bz;  // Controlled_Buffer controlled_buffer_4
  Register #(.width(5), .trigger("falling")) data_register (
    .D(DATA_IN), .Q(data_register_q), .clk(_12));  // open: en, clr
  Register #(.width(5)) ALUREG (.D(alu_1_result), .Q(ALUREG_q), .clk(_19));  // open: en, clr
  assign controlled_buffer_1_out = _7 ? ALUREG_q : 5'bz;  // Controlled_Buffer controlled_buffer_5
  Register #(.width(1)) FLAG (.D(alu_1_flag), .Q(FLAG_q), .clk(_19));  // open: en, clr
  Register #(.width(1)) FLAG_Z (.D(alu_1_flag_z), .Q(FLAG_Z_q), .clk(_19));  // open: en, clr
  LED LD_PC (.in(_10));
  LED PC_plus_plus (.in(_9));
  LED BUS__Dout (.in(_22));
  LED BUS__B (.in(_21));
  LED BUS__IR (.in(_11));
  LED PC_COUNT (.in(_23));
  controllo Test (
    .Flag(FLAG_q), .Flag_z(FLAG_Z_q), .out(Test_out),
    .disabilita_altra_entrata_1___no__0___si(Test_disabilita_altra_entrata_1___no__0___si), .not_eq(_29),
    .eq(_28), .pos(_20), .neg(_24));
  assign controlled_buffer_6_out = Test_disabilita_altra_entrata_1___no__0___si ? _10 : 1'bz;  // Controlled_Buffer controlled_buffer_6
  assign controlled_buffer_7_out = Test_disabilita_altra_entrata_1___no__0___si ? _23 : 1'bz;  // Controlled_Buffer controlled_buffer_7
  LED Din__DR (.in(_12));
  LED u__0 (.in(_24));
  not not_1 (not_1_out, Test_disabilita_altra_entrata_1___no__0___si);
  assign controlled_buffer_8_out = not_1_out ? Test_out : 1'bz;  // Controlled_Buffer controlled_buffer_8
  Counter #(.width(5), .max('h1f)) Program_Counter (
    .load(controlled_buffer_6_out), .D(controlled_buffer_1_out), .count(controlled_buffer_7_out),
    .Q(ADDRESS), .clk(_9), .clr(RESET));  // open: carry
  assign controlled_buffer_6_out = not_1_out ? Test_out : 1'bz;  // Controlled_Buffer controlled_buffer_9
  not not_2 (not_2_out, controlled_buffer_8_out);
  assign controlled_buffer_7_out = not_1_out ? not_2_out : 1'bz;  // Controlled_Buffer controlled_buffer_10
  assign DATA_OUT = _22 ? controlled_buffer_1_out : 5'bz;  // Controlled_Buffer controlled_buffer_11

  // Other names for the same wires on the sheet: _15 = MREQ; _16 = READ; _17 = IOREQ; _18 = WR

  // Notes on the sheet:
  //   β2015 - V. 1.3
  //   Internal Data Bus
endmodule

module Control_Unit (
  input  Internal_clock,
  input  Reset,
  input  [4:0] Op_Code,
  output [3:0] CU_COUNTER,
  output [31:0] Control_Output
);

  Counter #(.width(4), .max('hf)) counter_1 (
    .Q(CU_COUNTER), .clk(Internal_clock), .clr(Reset));  // open: load, D, count, carry
  ROM #(.addrWidth(9), .dataWidth(32)) rom_1 (.addr({Op_Code, CU_COUNTER}), .data(Control_Output));

  // Notes on the sheet:
  //   contents of rom_1 (hex, n*v repeats v):
  //   61000 62800 66000 13*0 861000 861200 7a000 7a040 861000 861200 78000 7a800 7e000 7*0 78008 78048
  //   861000 861200 78000 7a800 7e000 9*0 78002 78042 861000 861200 78000 7a800 7e000 9*0 78020 278020
  //   861000 861200 78000 7a800 7e000 9*0 78020 78024 861000 861200 78000 7a800 7e000 9*0 78008 78009
  //   f8080 780c0 861000 861200 78000 7a800 7e000 7*0 78002 78003 f8080 780c0 861000 861200 78000 7a800
  //   7e000 7*0 78002 78013 f8090 780c0 861000 861200 78000 7a800 7e000 7*0 78008 78109 f8180 278080
  //   861000 861200 78000 7a800 7e000 7*0 78008 78119 f8190 278080 861000 861200 78000 7a800 7e000 7*0
  //   878000 878200 63000 62000 63400 63600 78000 7a800 7e000 7*0 48000 49000 48000 7a000 7a040 861000
  //   861200 78000 7a800 7e000 6*0 418020 478020 861000 861200 78000 7a800 7e000 9*0 878000 878200 63000
  //   62000 163000 163200 78000 7a800 7e000 7*0 878000 878200 63000 62000 1023000 1023200 78000 7a800
  //   7e000 7*0 11111111 15*0 11111111 15*0 11111111 15*0 11111111 15*0 878000 878200 63000 62000 10063000
  //   10063200 78000 7a800 7e800 7*0 87800 878200 63000 62000 20063000 20063200 78000 7a800 7e800
endmodule

module ALU (
  input  [4:0] OP1,
  input  [4:0] OP2,
  input  [1:0] op,
  output [4:0] Result,
  output Flag_z,
  output Flag
);

  wire decoder_1_out0, decoder_1_out1, decoder_1_out2, decoder_1_out3;
  wire [4:0] adder_1_out, adder_2_out, subtractor_1_out, subtractor_2_out;

  Decoder #(.select(2)) decoder_1 (
    .out0(decoder_1_out0), .out1(decoder_1_out1), .out2(decoder_1_out2), .out3(decoder_1_out3), .sel(op));  // open: en
  Adder #(.width(5)) adder_1 (.a(OP1), .b(OP2), .out(adder_1_out));  // open: cin, cout
  assign {Flag, Result[3:0]} = decoder_1_out0 ? adder_1_out : 5'bz;  // Controlled_Buffer controlled_buffer_1
  Subtractor #(.width(5)) subtractor_1 (.a(OP1), .b(OP2), .out(subtractor_1_out));  // open: bin, bout
  assign {Flag, Result[3:0]} = decoder_1_out1 ? subtractor_1_out : 5'bz;  // Controlled_Buffer controlled_buffer_2
  Adder #(.width(5)) adder_2 (.a(OP2), .b(5'b00001), .out(adder_2_out));  // open: cin, cout
  Subtractor #(.width(5)) subtractor_2 (.a(OP2), .b(5'b00001), .out(subtractor_2_out));  // open: bin, bout
  assign {Flag, Result[3:0]} = decoder_1_out2 ? adder_2_out : 5'bz;  // Controlled_Buffer controlled_buffer_3
  assign {Flag, Result[3:0]} = decoder_1_out3 ? subtractor_2_out : 5'bz;  // Controlled_Buffer controlled_buffer_4
  Comparator #(.width(5)) comparator_1 (.a({Flag, Result[3:0]}), .b({5{1'b0}}), .eq(Flag_z));  // open: gt, lt

  assign Result[4] = Flag;

  // Notes on the sheet:
  //   00 somma - 01 sottrazione - 10 inc - 11 dec
endmodule

module controllo (
  input  Flag,
  input  Flag_z,
  input  not_eq,
  input  eq,
  input  pos,
  input  neg,
  output disabilita_altra_entrata_1___no__0___si,
  output out
);

  wire comparator_1_eq, comparator_2_eq, comparator_3_eq, comparator_4_eq;

  Comparator #(.width(1)) comparator_1 (.a(Flag), .b(1'b1), .eq(comparator_1_eq));  // open: gt, lt
  assign out = neg ? comparator_1_eq : 1'bz;  // Controlled_Buffer controlled_buffer_1
  Comparator #(.width(1)) comparator_2 (.a(Flag), .b(1'b0), .eq(comparator_2_eq));  // open: gt, lt
  assign out = eq ? comparator_4_eq : 1'bz;  // Controlled_Buffer controlled_buffer_2
  assign out = pos ? comparator_2_eq : 1'bz;  // Controlled_Buffer controlled_buffer_3
  Comparator #(.width(1)) comparator_3 (.a(Flag_z), .b(1'b0), .eq(comparator_3_eq));  // open: gt, lt
  Comparator #(.width(1)) comparator_4 (.a(Flag_z), .b(1'b1), .eq(comparator_4_eq));  // open: gt, lt
  assign out = not_eq ? comparator_3_eq : 1'bz;  // Controlled_Buffer controlled_buffer_4
  nor nor_1 (disabilita_altra_entrata_1___no__0___si, not_eq, pos, eq, neg);
endmodule
